# Fritzing sketch motor-board (saved by Fritzing 0.9.3b)
breadboards: 1

parts:
  M1 = DC Motor
  J1 = ATX24 Pin Power Supply Connector [package=atx24_right_angle]
  Composant2 = Arduino Nano (Rev3.0) (ICSP)
  Composant1 = Monster Moto Shield

nets:
  N1: M1.pin_1, Composant1.OUTA1
  N2: M1.pin_2, Composant1.OUTB1
  GND: J1.GND, Composant2.GND, Composant1.GND, Composant1.GND_-_GND@0, Composant1.GND_-_GND@1
  12V: J1.12V, Composant1.VCC
  N3: Composant2.D5, Composant1.PWM1_-_D5
  N4: Composant2.D7, Composant1.INA1_-_D7
  N5: Composant2.D8, Composant1.INB1_-_D8
  5V: Composant2.5V, Composant1.5V
  N6: Composant2.A2, Composant1.CS1_-_A2
  N7: Composant2.A0, Composant1.EN1_-_A0

notes:
  VNH2SP30 board
  ATX 12V power supply
